# Fritzing sketch braking_schematic (saved by Fritzing 0.9.2b)

parts:
  Microcontroller = PIC16F88-DIP [package=dil18]
  Front_Brake_Motor = DC Motor
  Back_Brake_Lever_Motor = DC Motor
  Right_Brake_Lever = Rotary Potentiometer (Small) [maximum_resistance=100kΩ package=THT]
  Left_Brake_Lever = Rotary Potentiometer (Small) [package=THT]
  GND = Screw terminal - 2 pins [package=THT]
  5V = Screw terminal - 2 pins [package=THT]

nets:
  N1: Microcontroller.RA2_AN2, Front_Brake_Motor.pin_1
  N2: Microcontroller.RA3_AN3, Back_Brake_Lever_Motor.pin_1
  N3: Microcontroller.VSS, Front_Brake_Motor.pin_2, Right_Brake_Lever.leg1, Left_Brake_Lever.leg1, GND.pin1, 5V.pin1
  N4: Microcontroller.VDD, Right_Brake_Lever.leg2, Left_Brake_Lever.leg2, GND.pin2, 5V.pin2
  N5: Microcontroller.RA0_AN0, Right_Brake_Lever.wiper
  N6: Microcontroller.RA1_AN1, Left_Brake_Lever.wiper
